// Logisim project cpu.circ as structural Verilog: 4 circuits, main circuit main
module main (
  input  [15:0] INSTRUCTION,
  input  CLOCK,
  output [15:0] FETCH_ADDRESS,
  output [15:0] s0_Value,
  output [15:0] s1_Value,
  output [15:0] s2_Value,
  output [15:0] ra_Value,
  output [15:0] sp_Value,
  output [15:0] HI_Value,
  output [15:0] LO_Value
);

  wire ALUSrc, beq_bne, Branch, BranchTrue, ExtOp, ImmCtr, Jump, LOCtr, main_2_equal, MemToReg, MemWr,
       multiplexer_9_out, not_1_out, or_1_out, or_2_out, RegDst, RegWr, RT_RD, WrHi, WrLo;
  wire [1:0] HILOCtr, PCCtr;
  wire [2:0] ALUCtr, multiplexer_5_out, multiplexer_6_out, U_rd;
  wire [15:0] adder_1_out, adder_3_out, BResult, EX_INSTRUCTION, EX_PC, I_Ext, LOData, MEM_p5,
       multiplexer_2_out, multiplexer_4_out, multiplexer_7_out, multiplexer_8_out, multiplexer_10_out,
       multiplexer_11_out, newPC, Result, Result2, RF_rs, RF_rt, shifter_1_out, U_Ext, WriteData;

  Adder #(.width(16)) adder_1 (.a(FETCH_ADDRESS), .b(16'h2), .out(adder_1_out));  // open: cin, cout
  or or_1 (or_1_out, BranchTrue, Jump);
  Register #(.width(16)) HI (.D(Result2), .en(WrHi), .Q(HI_Value), .clk(CLOCK));  // open: clr
  Multiplexer #(.width(16), .enable("false")) multiplexer_1 (
    .in0(Result), .in1(shifter_1_out), .out(LOData), .sel(LOCtr));
  Shifter #(.width(16)) shifter_1 (.in(U_Ext), .\dist (4'b0110), .out(shifter_1_out));
  // Probe on shifter_1_out
  // Probe on multiplexer_2_out
  Multiplexer #(.width(16), .enable("false")) multiplexer_2 (
    .in0(adder_1_out), .in1(newPC), .out(multiplexer_2_out), .sel(or_1_out));
  // Probe on newPC
  Multiplexer #(.select(2), .width(16), .enable("false")) multiplexer_3 (
    .in0({EX_PC[15:10], EX_INSTRUCTION[9:0]}), .in1(Result), .in2(BResult), .out(newPC), .sel(PCCtr));  // open: in3
  // Probe on PCCtr
  Register #(.width(16)) PC (.D(multiplexer_2_out), .en(1'b1), .Q(FETCH_ADDRESS), .clk(CLOCK));  // open: clr
  // Probe on LO_Value
  Register #(.width(16)) LO (.D(LOData), .en(WrLo), .Q(LO_Value), .clk(CLOCK));  // open: clr
  // Probe on INSTRUCTION
  or or_2 (or_2_out, Jump, BranchTrue);
  Register #(.width(16)) u_EX_PC (.D(FETCH_ADDRESS), .en(1'b1), .Q(EX_PC), .clk(CLOCK));  // open: clr
  Multiplexer #(.width(16), .enable("false")) multiplexer_4 (
    .in0(INSTRUCTION), .in1({16{1'b0}}), .out(multiplexer_4_out), .sel(or_2_out));
  Register #(.width(16)) Instruction_Register (
    .D(multiplexer_4_out), .en(1'b1), .Q(EX_INSTRUCTION), .clk(CLOCK));  // open: clr
  // Probe on ALUCtr
  Control control_1 (
    .Funct(EX_INSTRUCTION[2:0]), .Opcode(EX_INSTRUCTION[15:12]), .ALUCtr(ALUCtr), .RegDst(RegDst),
    .ExtOp(ExtOp), .RegWr(RegWr), .ALUSrc(ALUSrc), .MemWr(MemWr), .MemToReg(MemToReg), .Jump(Jump),
    .Branch(Branch), ._0_____I___1___U(ImmCtr), .WrHI(WrHi), .WrLO(WrLo));
  Ext ext_1 (.in_1(EX_INSTRUCTION[5:0]), .in_2(EX_INSTRUCTION[9:0]), .in_3(ExtOp), .I_Ext(I_Ext), .U_Ext(U_Ext));
  // Probe on EX_INSTRUCTION
  Control2 control2_1 (
    .Funct(EX_INSTRUCTION[2:0]), .Opcode(EX_INSTRUCTION[15:12]), .HILOCtr(HILOCtr), .RT_RD(RT_RD),
    .LOCtr(LOCtr), .PCCtr(PCCtr), .beq_bne(beq_bne));
  // Probe on EX_INSTRUCTION[11:9]
  // Probe on EX_INSTRUCTION[15:12]
  assign U_rd = {{1{1'b0}}, EX_INSTRUCTION[11:10]};  // Bit_Extender bit_extender_1
  // Probe on EX_INSTRUCTION[5:0]
  // Probe on EX_INSTRUCTION[9:0]
  // Probe on U_rd
  Multiplexer #(.width(3), .enable("false")) multiplexer_5 (
    .in0(EX_INSTRUCTION[5:3]), .in1(EX_INSTRUCTION[11:9]), .out(multiplexer_5_out), .sel(RT_RD));
  // Probe on multiplexer_6_out
  Multiplexer #(.width(3), .enable("false")) multiplexer_6 (
    .in0(EX_INSTRUCTION[11:9]), .in1(U_rd), .out(multiplexer_6_out), .sel(RegDst));
  regfile_main main_1 (
    .Read_Register_1(EX_INSTRUCTION[8:6]), .Read_Register_2(multiplexer_5_out),
    .Write_Register(multiplexer_6_out), .Write_Data(WriteData), .Write_Enable(RegWr), .Clock(CLOCK),
    .Read_Data_1(RF_rs), .Read_Data_2(RF_rt), .s0_Value(s0_Value), .s1_Value(s1_Value), .s2_Value(s2_Value),
    .ra_Value(ra_Value), .sp_Value(sp_Value));
  Multiplexer #(.width(16), .enable("false")) multiplexer_7 (
    .in0(RF_rt), .in1(multiplexer_8_out), .out(multiplexer_7_out), .sel(ALUSrc));
  Multiplexer #(.width(16), .enable("false")) multiplexer_8 (
    .in0(I_Ext), .in1(U_Ext), .out(multiplexer_8_out), .sel(ImmCtr));
  // Probe on RF_rs
  alu_main main_2 (
    .Switch(ALUCtr), .X(RF_rs), .Equal(main_2_equal), .Result(Result), .Y(multiplexer_7_out),
    .Result_2(Result2));
  // Probe on multiplexer_7_out
  // Probe on EX_PC
  // Probe on I_Ext
  Multiplexer #(.enable("false")) multiplexer_9 (
    .in0(main_2_equal), .in1(not_1_out), .out(multiplexer_9_out), .sel(beq_bne));
  not not_1 (not_1_out, main_2_equal);
  // Probe on Result
  // Probe on Result2
  // Probe on BResult
  Adder #(.width(16)) adder_2 (.a(EX_PC), .b(I_Ext), .out(BResult));  // open: cin, cout
  and and_1 (BranchTrue, multiplexer_9_out, Branch);
  Multiplexer #(.select(2), .width(16), .enable("false")) multiplexer_10 (
    .in0(Result), .in1(Result), .in2(HI_Value), .in3(LO_Value), .out(multiplexer_10_out), .sel(HILOCtr));
  // mem_main MEM: pin names not known; wires that end beside it: Result, RF_rt, MemWr, CLOCK, MEM_p5
  // Probe on multiplexer_11_out
  Multiplexer #(.width(16), .enable("false")) multiplexer_11 (
    .in0(multiplexer_10_out), .in1(MEM_p5), .out(multiplexer_11_out), .sel(MemToReg));
  Adder #(.width(16)) adder_3 (.a(EX_PC), .b(16'h2), .out(adder_3_out));  // open: cin, cout
  Multiplexer #(.width(16), .enable("false")) multiplexer_12 (
    .in0(multiplexer_11_out), .in1(adder_3_out), .out(WriteData), .sel(Jump));

  // Other names for the same wires on the sheet: clk = CLOCK; funct[2:0] = EX_INSTRUCTION[2:0];
  //   I_Imm[5:0] = EX_INSTRUCTION[5:0]; U_imm[9:0] = EX_INSTRUCTION[9:0]; rt[2:0] = EX_INSTRUCTION[5:3];
  //   rs[2:0] = EX_INSTRUCTION[8:6]; rd[2:0] = EX_INSTRUCTION[11:9]; Opcode[3:0] = EX_INSTRUCTION[15:12];
  //   fetch_addr[15:0] = FETCH_ADDRESS; HI[15:0] = HI_Value; LO[15:0] = LO_Value; ra[15:0] = ra_Value;
  //   s0[15:0] = s0_Value; s1[15:0] = s1_Value; s2[15:0] = s2_Value; sp[15:0] = sp_Value

  // Notes on the sheet:
  //   fetch_addr
  //   Output
  //   jump logic
  //   PC Logic
  //   These are outputs/inputs from run.circ
  //   Inputs
  //   lui
  //   Pipeline Logic
  //   Control
  //   These are DEBUG/TEST outputs from your circuit.
  //   PC is incremented every stage, but the execute stage is delayed so we must keep the old PC value
  //   We don't need two registers
  //   Sign/Zero Extender
  //   0 = j, 1 = jr
  //   0 = beq, 1 = bne
  //   special case of sw, need to change read register because of differences between U and I type
  //   fetch_addr
  //   EX
  //   Branch Logic and Calculation
  //   MEM
  //   fetch_addr
  //   Special case for jump, where R[rd] = PC +2
endmodule

module Control (
  input  [2:0] Funct,
  input  [3:0] Opcode,
  output [2:0] ALUCtr,
  output RegDst,
  output ExtOp,
  output RegWr,
  output ALUSrc,
  output MemWr,
  output MemToReg,
  output Jump,
  output Branch,
  output _0_____I___1___U,
  output WrHI,
  output WrLO
);

  wire comparator_2_eq, comparator_3_eq, I_Type, multiplexer_7_out, multiplexer_12_out, multiplexer_15_out,
       R_Type, U_Type;
  wire [2:0] multiplexer_1_out, multiplexer_5_out;

  // Probe on R_Type
  Comparator #(.width(4), .mode("unsigned")) comparator_1 (.a(4'b0000), .b(Opcode), .eq(R_Type));  // open: gt, lt
  // Probe on comparator_2_eq
  Comparator #(.width(4), .mode("unsigned")) comparator_2 (
    .a(4'b0001), .b(Opcode), .eq(comparator_2_eq));  // open: gt, lt
  // Probe on comparator_3_eq
  Comparator #(.width(4), .mode("unsigned")) comparator_3 (
    .a(4'b0010), .b(Opcode), .eq(comparator_3_eq));  // open: gt, lt
  // Probe on I_Type
  Comparator #(.width(4), .mode("unsigned")) comparator_4 (.a(4'b0010), .b(Opcode), .lt(I_Type));  // open: gt, eq
  // Probe on U_Type
  or or_1 (U_Type, comparator_2_eq, comparator_3_eq);
  Multiplexer #(.select(4), .width(3), .enable("false")) multiplexer_1 (
    .in0(Funct), .in1(3'b010), .in2(3'b010), .in3(3'b010), .in4(3'b010), .in5(3'b010), .in6(3'b010),
    .in7(3'b110), .in8(3'b011), .in9(3'b100), .in10(3'b010), .in11(3'b010), .in12(3'b010), .in13(3'b010),
    .in14(3'b010), .in15(3'b010), .out(multiplexer_1_out), .sel(Opcode));
  Multiplexer #(.select(4), .enable("false")) multiplexer_2 (
    .in0(1'b0), .in1(1'b0), .in2(1'b0), .in3(1'b1), .in4(1'b1), .in5(1'b1), .in6(1'b1), .in7(1'b1),
    .in8(1'b0), .in9(1'b0), .in10(1'b1), .in11(1'b1), .in12(1'b0), .in13(1'b0), .in14(1'b0), .in15(1'b0),
    .out(ExtOp), .sel(Opcode));
  Multiplexer #(.select(4), .enable("false")) multiplexer_3 (
    .in0(1'b0), .in1(1'b0), .in2(1'b0), .in3(1'b0), .in4(1'b0), .in5(1'b0), .in6(1'b0), .in7(1'b0),
    .in8(1'b0), .in9(1'b0), .in10(1'b1), .in11(1'b0), .in12(1'b0), .in13(1'b0), .in14(1'b0), .in15(1'b0),
    .out(MemToReg), .sel(Opcode));
  Multiplexer #(.select(4), .enable("false")) multiplexer_4 (
    .in0(1'b0), .in1(1'b0), .in2(1'b0), .in3(1'b1), .in4(1'b0), .in5(1'b0), .in6(1'b1), .in7(1'b1),
    .in8(1'b1), .in9(1'b1), .in10(1'b1), .in11(1'b1), .in12(1'b0), .in13(1'b0), .in14(1'b0), .in15(1'b0),
    .out(ALUSrc), .sel(Opcode));
  Multiplexer #(.width(3), .enable("false")) multiplexer_5 (
    .in0(multiplexer_1_out), .in1(3'b010), .out(multiplexer_5_out), .sel(U_Type));
  Multiplexer #(.width(3), .enable("false")) multiplexer_6 (
    .in0(multiplexer_5_out), .in1(Funct), .out(ALUCtr), .sel(R_Type));
  Multiplexer #(.select(3), .enable("false")) multiplexer_7 (
    .in0(1'b1), .in1(1'b1), .in2(1'b1), .in3(1'b1), .in4(1'b1), .in5(1'b1), .in6(1'b1), .in7(1'b0),
    .out(multiplexer_7_out), .sel(Funct));
  Multiplexer #(.select(4), .enable("false")) multiplexer_8 (
    .in0(1'b0), .in1(1'b0), .in2(1'b1), .in3(1'b1), .in4(1'b0), .in5(1'b0), .in6(1'b0), .in7(1'b0),
    .in8(1'b0), .in9(1'b0), .in10(1'b0), .in11(1'b0), .in12(1'b0), .in13(1'b0), .in14(1'b0), .in15(1'b0),
    .out(Jump), .sel(Opcode));
  Multiplexer #(.select(4), .enable("false")) multiplexer_9 (
    .in0(multiplexer_7_out), .in1(1'b0), .in2(1'b1), .in3(1'b1), .in4(1'b0), .in5(1'b0), .in6(1'b1),
    .in7(1'b1), .in8(1'b1), .in9(1'b1), .in10(1'b1), .in11(1'b0), .in12(1'b1), .in13(1'b1), .in14(1'b0),
    .in15(1'b0), .out(RegWr), .sel(Opcode));
  Multiplexer #(.select(4), .enable("false")) multiplexer_10 (
    .in0(1'b0), .in1(1'b0), .in2(1'b0), .in3(1'b0), .in4(1'b0), .in5(1'b0), .in6(1'b0), .in7(1'b0),
    .in8(1'b0), .in9(1'b0), .in10(1'b0), .in11(1'b1), .in12(1'b0), .in13(1'b0), .in14(1'b0), .in15(1'b0),
    .out(MemWr), .sel(Opcode));
  Multiplexer #(.select(4), .enable("false")) multiplexer_11 (
    .in0(1'b0), .in1(1'b0), .in2(1'b0), .in3(1'b0), .in4(1'b1), .in5(1'b1), .in6(1'b0), .in7(1'b0),
    .in8(1'b0), .in9(1'b0), .in10(1'b0), .in11(1'b0), .in12(1'b0), .in13(1'b0), .in14(1'b0), .in15(1'b0),
    .out(Branch), .sel(Opcode));
  Multiplexer #(.select(3), .enable("false")) multiplexer_12 (
    .in0(1'b0), .in1(1'b0), .in2(1'b0), .in3(1'b0), .in4(1'b0), .in5(1'b0), .in6(1'b0), .in7(1'b1),
    .out(multiplexer_12_out), .sel(Funct));
  Multiplexer #(.select(4), .enable("false")) multiplexer_13 (
    .in0(1'b0), .in1(1'b1), .in2(1'b1), .in3(1'b0), .in4(1'b0), .in5(1'b0), .in6(1'b0), .in7(1'b0),
    .in8(1'b0), .in9(1'b0), .in10(1'b0), .in11(1'b0), .in12(1'b0), .in13(1'b0), .in14(1'b0), .in15(1'b0),
    .out(RegDst), .sel(Opcode));
  Multiplexer #(.select(4), .enable("false")) multiplexer_14 (
    .in0(1'b0), .in1(1'b1), .in2(1'b1), .in3(1'b0), .in4(1'b0), .in5(1'b0), .in6(1'b0), .in7(1'b0),
    .in8(1'b0), .in9(1'b0), .in10(1'b0), .in11(1'b0), .in12(1'b0), .in13(1'b0), .in14(1'b0), .in15(1'b0),
    .out(_0_____I___1___U), .sel(Opcode));
  Multiplexer #(.select(3), .enable("false")) multiplexer_15 (
    .in0(1'b0), .in1(1'b0), .in2(1'b0), .in3(1'b0), .in4(1'b0), .in5(1'b0), .in6(1'b0), .in7(1'b1),
    .out(multiplexer_15_out), .sel(Funct));
  Multiplexer #(.select(4), .enable("false")) multiplexer_16 (
    .in0(multiplexer_12_out), .in1(1'b0), .in2(1'b0), .in3(1'b0), .in4(1'b0), .in5(1'b0), .in6(1'b0),
    .in7(1'b0), .in8(1'b0), .in9(1'b0), .in10(1'b0), .in11(1'b0), .in12(1'b0), .in13(1'b0), .in14(1'b0),
    .in15(1'b0), .out(WrHI), .sel(Opcode));
  Multiplexer #(.select(4), .enable("false")) multiplexer_17 (
    .in0(multiplexer_15_out), .in1(1'b1), .in2(1'b0), .in3(1'b0), .in4(1'b0), .in5(1'b0), .in6(1'b0),
    .in7(1'b0), .in8(1'b0), .in9(1'b0), .in10(1'b0), .in11(1'b0), .in12(1'b0), .in13(1'b0), .in14(1'b0),
    .in15(1'b0), .out(WrLO), .sel(Opcode));

  // Other names for the same wires on the sheet: Imm_Ctrl = _0_____I___1___U

  // Notes on the sheet:
  //   Inputs
  //   Outputs
  //   add for branch
  //   NOP for mfhi and mflo
  //   Last Two Opcodes Don't Exist
  //   R-type, lui, jump
  //   jr, beq, bne, addi, slti
  //   andi, ori
  //   lh, sh
  //   mfhi, mflo, 2 nop
  //   addi, slti, andi, ori, lh, sh
  //   everything else
  //   RTypes, lui, j
  //   jr
  //   beq, bne
  //   mfhi, mflo
  //   nop
  //   lh
  //   mfhi, mflo
  //   nop
  //   NOP for Jump and LUI, set as add
  //   NOP for Jump and LUI, set as add
  //   beq, bne
  //   sh
  //   mfhi,mflo
  //   2 nop
  //   j, jr
  //   everything else
  //   lui
  //   everything else
  //   sh
  //   mfhi, mflo
  //   nop
  //   RTypes, lui
  //   mult writes to LO HI, lui writes to LO, beq bne only changes PC, sw doesn't write
  //   Rtypes, lui, j, jr
  //   beq, bne
  //   everything else
  //   RType
  //   lui,j 
  //   everything else
  //   mfhi,mflo
  //   2 nop
  //   RType
  //   lui, j (UTypes)
  //   ITypes
  //   Only Mult
  //   Everything else
  //   mfhi
  //   mflo, 2 nops
  //   lui
  //   everything else
  //   mflo
  //   2  nops
endmodule

module Ext (
  input  [5:0] in_1,
  input  [9:0] in_2,
  input  in_3,
  output [15:0] I_Ext,
  output [15:0] U_Ext
);

  wire [15:0] bit_extender_1_out, bit_extender_2_out, bit_extender_3_out, bit_extender_4_out;

  assign bit_extender_1_out = {{10{1'b0}}, in_1};  // Bit_Extender bit_extender_1
  assign bit_extender_2_out = {{10{in_1[5]}}, in_1};  // Bit_Extender bit_extender_2
  assign bit_extender_3_out = {{6{1'b0}}, in_2};  // Bit_Extender bit_extender_3
  Multiplexer #(.width(16), .enable("false")) multiplexer_1 (
    .in0(bit_extender_3_out), .in1(bit_extender_4_out), .out(U_Ext), .sel(in_3));
  assign bit_extender_4_out = {{6{in_2[9]}}, in_2};  // Bit_Extender bit_extender_4
  Multiplexer #(.width(16), .enable("false")) multiplexer_2 (
    .in0(bit_extender_1_out), .in1(bit_extender_2_out), .out(I_Ext), .sel(in_3));

  // Other names for the same wires on the sheet: ExtOp = in_3; I_Imm[5:0] = in_1; U_Imm[9:0] = in_2

  // Notes on the sheet:
  //   I_Imm
  //   U_Imm
  //   ExtOp
endmodule

module Control2 (
  input  [2:0] Funct,
  input  [3:0] Opcode,
  output [1:0] HILOCtr,
  output RT_RD,
  output LOCtr,
  output [1:0] PCCtr,
  output beq_bne
);

  Multiplexer #(.select(4), .width(2), .enable("false")) multiplexer_1 (
    .in0(2'b00), .in1(2'b00), .in2(2'b00), .in3(2'b01), .in4(2'b10), .in5(2'b10), .in6(2'b00), .in7(2'b00),
    .in8(2'b00), .in9(2'b00), .in10(2'b00), .in11(2'b00), .in12(2'b00), .in13(2'b00), .in14(2'b00),
    .in15(2'b00), .out(PCCtr), .sel(Opcode));
  Multiplexer #(.select(4), .enable("false")) multiplexer_2 (
    .in0(1'b0), .in1(1'b0), .in2(1'b0), .in3(1'b0), .in4(1'b1), .in5(1'b1), .in6(1'b0), .in7(1'b0),
    .in8(1'b0), .in9(1'b0), .in10(1'b0), .in11(1'b1), .in12(1'b0), .in13(1'b0), .in14(1'b0), .in15(1'b0),
    .out(RT_RD), .sel(Opcode));
  Multiplexer #(.select(4), .enable("false")) multiplexer_3 (
    .in0(1'b0), .in1(1'b0), .in2(1'b0), .in3(1'b0), .in4(1'b0), .in5(1'b1), .in6(1'b0), .in7(1'b0),
    .in8(1'b0), .in9(1'b0), .in10(1'b0), .in11(1'b0), .in12(1'b0), .in13(1'b0), .in14(1'b0), .in15(1'b0),
    .out(beq_bne), .sel(Opcode));
  Multiplexer #(.select(4), .width(2), .enable("false")) multiplexer_4 (
    .in0(2'b00), .in1(2'b00), .in2(2'b00), .in3(2'b00), .in4(2'b00), .in5(2'b00), .in6(2'b00), .in7(2'b00),
    .in8(2'b00), .in9(2'b00), .in10(2'b00), .in11(2'b00), .in12(2'b10), .in13(2'b11), .in14(2'b00),
    .in15(2'b00), .out(HILOCtr), .sel(Opcode));
  Multiplexer #(.select(4), .enable("false")) multiplexer_5 (
    .in0(1'b0), .in1(1'b1), .in2(1'b0), .in3(1'b0), .in4(1'b0), .in5(1'b0), .in6(1'b0), .in7(1'b0),
    .in8(1'b0), .in9(1'b0), .in10(1'b0), .in11(1'b0), .in12(1'b0), .in13(1'b0), .in14(1'b0), .in15(1'b0),
    .out(LOCtr), .sel(Opcode));

  // Notes on the sheet:
  //   Inputs
  //   j
  //   jr
  //   beq, bne
  //   nop
  //   0 = jump, 1 = jr, 2 = branch
  //   everything else
  //   sh
  //   mfhi, mflo
  //   2 nops
  //   beq/nop
  //   bne
  //   nop
  //   Everything else is result
  //   high = 2
  //   low = 3
  //   nops
  //   lui
  //   may need to edit this later for j/branch
endmodule
