// Logisim project regfile.circ as structural Verilog: 1 circuit, main circuit main
module main (
  input  [2:0] Read_Register_1,
  input  [2:0] Read_Register_2,
  input  [2:0] Write_Register,
  input  [15:0] Write_Data,
  input  Write_Enable,
  input  Clock,
  output [15:0] s0_Value,
  output [15:0] s1_Value,
  output [15:0] s2_Value,
  output [15:0] ra_Value,
  output [15:0] sp_Value,
  output [15:0] Read_Data_1,
  output [15:0] Read_Data_2
);

  wire _0_en, a0_en, ra_en, s0_en, s1_en, s2_en, sp_en, v0_en;
  wire [15:0] _0, _0_write, a0, a0_write, ra_write, s0_write, s1_write, s2_write, sp_write, v0, v0_write;

  Demultiplexer #(.select(3), .enable("false")) demultiplexer_1 (
    .out0(_0_en), .out1(ra_en), .out2(s0_en), .out3(s1_en), .out4(s2_en), .out5(a0_en), .out6(v0_en),
    .out7(sp_en), .in(Write_Enable), .sel(Write_Register));
  Multiplexer #(.select(3), .width(16), .enable("false")) multiplexer_1 (
    .in0(_0), .in1(ra_Value), .in2(s0_Value), .in3(s1_Value), .in4(s2_Value), .in5(a0), .in6(v0),
    .in7(sp_Value), .out(Read_Data_1), .sel(Read_Register_1));
  Register #(.width(16)) u__0 (.Q(_0), .clk(Clock));  // open: D, en, clr
  Register #(.width(16)) _1__ra (.D(ra_write), .en(ra_en), .Q(ra_Value), .clk(Clock));  // open: clr
  Register #(.width(16)) _2__s0 (.D(s0_write), .en(s0_en), .Q(s0_Value), .clk(Clock));  // open: clr
  Register #(.width(16)) _3__s1 (.D(s1_write), .en(s1_en), .Q(s1_Value), .clk(Clock));  // open: clr
  Register #(.width(16)) _4__s2 (.D(s2_write), .en(s2_en), .Q(s2_Value), .clk(Clock));  // open: clr
  Register #(.width(16)) _5__a0 (.D(a0_write), .en(a0_en), .Q(a0), .clk(Clock));  // open: clr
  Register #(.width(16)) _6__v0 (.D(v0_write), .en(v0_en), .Q(v0), .clk(Clock));  // open: clr
  Register #(.width(16)) _7__sp (.D(sp_write), .en(sp_en), .Q(sp_Value), .clk(Clock));  // open: clr
  Multiplexer #(.select(3), .width(16), .enable("false")) multiplexer_2 (
    .in0(_0), .in1(ra_Value), .in2(s0_Value), .in3(s1_Value), .in4(s2_Value), .in5(a0), .in6(v0),
    .in7(sp_Value), .out(Read_Data_2), .sel(Read_Register_2));
  Demultiplexer #(.select(3), .width(16), .enable("false")) demultiplexer_2 (
    .out0(_0_write), .out1(ra_write), .out2(s0_write), .out3(s1_write), .out4(s2_write), .out5(a0_write),
    .out6(v0_write), .out7(sp_write), .in(Write_Data), .sel(Write_Register));

  // Other names for the same wires on the sheet: clk = Clock; ra[15:0] = ra_Value; read_data1[15:0] = Read_Data_1;
  //   read_data2[15:0] = Read_Data_2; read_reg1[2:0] = Read_Register_1; read_reg2[2:0] = Read_Register_2;
  //   s0[15:0] = s0_Value; s1[15:0] = s1_Value; s2[15:0] = s2_Value; sp[15:0] = sp_Value; write_en = Write_Enable;
  //   write_reg[2:0] = Write_Register

  // Notes on the sheet:
  //   INPUTS to your circuit
  //   DON'T CHANGE THE LOCATIONS OF THE INPUTS AND OUTPUTS!
  //   These are DEBUG/TEST outputs from your circuit.
  //   OUTPUTS from your circuit
endmodule
